# Fritzing sketch Fritzing diagram (saved by Fritzing 0.9.3b)

parts:
  Part1 = Arduino Uno (Rev3) - ICSP
  LED1 = RGB LED (com. cathode, rgb) [package="5 mm [THT]"]
  Part2 = HX711 Weighing Sensor Module

nets:
  N1: Part1.D9_PWM, LED1.red_anode
  N2: Part1.D10_PWM/SS, LED1.common_cathode
  N3: Part1.D11_PWM/MOSI, LED1.green_anode
  N4: Part1.D2, Part2.CK/TX
  N5: Part1.D3_PWM, Part2.DO/RX
  5V: Part1.5V, Part2.VCC
  N6: Part1.VIN, LED1.blue_anode

notes:
  To load sensors
