# Fritzing sketch Prototype 1.0 Fritzing (saved by Fritzing 0.9.3b)

parts:
  Part1 = LilyPad Light Sensor
  Part2 = LilyPad Arduino Simple Board
  Part3 = LilyPad LED
  Part4 = LilyPad LED

nets:
  N1: Part1.+, Part2.VCC
  N2: Part1.-, Part2.GND, Part3.-, Part4.-
  N3: Part1.S, Part2.A3
  N4: Part2.D6, Part3.+
  N5: Part2.D5, Part4.+
